# Fritzing sketch montage10 (saved by Fritzing 0.7.10b)
breadboards: 1

parts:
  U1 = atmega328 [package=dip]
  XTAL3 = Crystal [frequency="16 Mhz" package=THT]
  C1 = Ceramic Capacitor [capacitance=100nF package="100 mil [THT, multilayer]"]
  C2 = Ceramic Capacitor [capacitance=100nF package="100 mil [THT, multilayer]"]
  R1 = Resistor [tolerance=±5% resistance=10k package=THT]
  7_Segment1 = 7 Segment Display
  R5 = Resistor [tolerance=±5% resistance=1k package=THT]
  R6 = Resistor [tolerance=±5% resistance=1k package=THT]
  R7 = Rotary Potentiometer (Small) [maximum_resistance=100kΩ]
  C11 = Electrolytic Capacitor [capacitance=1µF package="100 mil [THT, electrolytic]"]
  C12 = Electrolytic Capacitor [capacitance=1µF package="100 mil [THT, electrolytic]"]

nets:
  N1: U1.RESET, R1.Pin_1
  N2: U1.VCC, U1.AVCC, U1.A3, R1.Pin_0, R7.leg1, C11.-, C12.-
  N3: U1.GND, C1.0, C2.0, R5.Pin_0, R6.Pin_1, R7.leg2, C11.+, C12.+
  N4: U1.XLAT1, XTAL3.pin_0, C1.1
  N5: U1.XLAT2, XTAL3.pin_1, C2.1
  N6: U1.D5_(PWM), 7_Segment1.Segment_D
  N7: U1.D6_(PWM), 7_Segment1.Segment_E
  N8: U1.D7, 7_Segment1.Segment_F
  N9: U1.D8, 7_Segment1.Segment_A#1
  N10: U1.D11_(PWM), 7_Segment1.Segment_A#10
  N11: U1.D12, 7_Segment1.Segment_B
  N12: U1.D13, 7_Segment1.Segment_C
  N13: U1.A5, R7.wiper
  N14: 7_Segment1.common_cathode#3, R5.Pin_1
  N15: 7_Segment1.common_cathode#8, R6.Pin_0
