# Fritzing sketch montage3 (saved by Fritzing 0.7.10b)
breadboards: 1

parts:
  U1 = atmega328 [package=dip]
  XTAL3 = Crystal [frequency="16 Mhz" package=THT]
  C1 = Ceramic Capacitor [capacitance=100nF package="100 mil [THT, multilayer]"]
  C2 = Ceramic Capacitor [capacitance=100nF package="100 mil [THT, multilayer]"]
  R1 = Resistor [tolerance=±5% resistance=10k package=THT]
  R2 = Resistor [tolerance=±5% resistance=1k package=THT]
  LED1 = LED - 5mm [color="Red (635nm)" package="5 mm [THT]"]
  R3 = Rotary Potentiometer (Small) [maximum_resistance=100kΩ]
  C7 = Electrolytic Capacitor [capacitance=1µF package="100 mil [THT, electrolytic]"]
  C8 = Electrolytic Capacitor [capacitance=1µF package="100 mil [THT, electrolytic]"]

nets:
  N1: U1.RESET, R1.Pin_1
  N2: U1.D3_(PWM), LED1.anode
  N3: U1.VCC, U1.AVCC, R1.Pin_0, R3.leg1, C7.-, C8.-
  N4: U1.GND, C1.0, C2.0, R2.Pin_0, R3.leg2, C7.+, C8.+
  N5: U1.XLAT1, XTAL3.pin_0, C1.1
  N6: U1.XLAT2, XTAL3.pin_1, C2.1
  N7: U1.A5, R3.wiper
  N8: R2.Pin_1, LED1.cathode
