# Fritzing sketch montage6 (saved by Fritzing 0.7.10b)
breadboards: 1

parts:
  U1 = atmega328 [package=dip]
  XTAL3 = Crystal [frequency="16 Mhz" package=THT]
  C1 = Ceramic Capacitor [capacitance=100nF package="100 mil [THT, multilayer]"]
  C2 = Ceramic Capacitor [capacitance=100nF package="100 mil [THT, multilayer]"]
  R1 = Resistor [tolerance=±5% resistance=10k package=THT]
  R4 = Resistor [tolerance=±5% resistance=10k package=THT]
  C13 = Electrolytic Capacitor [capacitance=1µF package="100 mil [THT, electrolytic]"]
  C14 = Electrolytic Capacitor [capacitance=1µF package="100 mil [THT, electrolytic]"]
  J1 = Piezo Speaker
  R5 = Resistor [tolerance=±5% resistance=1k package=THT]

nets:
  N1: U1.RESET, R1.Pin_1
  N2: U1.VCC, U1.AVCC, R1.Pin_0, C13.-, C14.-
  N3: U1.GND, C1.0, C2.0, R4.Pin_1, C13.+, C14.+, R5.Pin_1
  N4: U1.XLAT1, XTAL3.pin_0, C1.1
  N5: U1.XLAT2, XTAL3.pin_1, C2.1
  N6: U1.D9_(PWM), J1.pin1
  N7: U1.A4, R4.Pin_0
  N8: J1.pin2, R5.Pin_0
