# Fritzing sketch montage7 (saved by Fritzing 0.7.10b)
breadboards: 1

parts:
  U1 = atmega328 [package=dip]
  XTAL3 = Crystal [frequency="16 Mhz" package=THT]
  C1 = Ceramic Capacitor [capacitance=100nF package="100 mil [THT, multilayer]"]
  C2 = Ceramic Capacitor [capacitance=100nF package="100 mil [THT, multilayer]"]
  R1 = Resistor [tolerance=±5% resistance=10k package=THT]
  Q1 = NPN-Transistor [package="TO92 [THT]"]
  MIC1 = Microphone
  R2 = Resistor [tolerance=±5% resistance=10k package=THT]
  LED1 = LED - 5mm [color="Red (633nm)" package="5 mm [THT]"]
  R3 = Resistor [tolerance=±5% resistance=1k package=THT]

nets:
  N1: U1.RESET, R1.Pin_1
  N2: U1.VCC, U1.AVCC, R1.Pin_0, Q1.C, MIC1.pin2
  N3: U1.GND, C1.0, C2.0, R2.Pin_1, R3.Pin_0
  N4: U1.XLAT1, XTAL3.pin_0, C1.1
  N5: U1.XLAT2, XTAL3.pin_1, C2.1
  N6: U1.A2, LED1.anode
  N7: U1.A3, Q1.E, R2.Pin_0
  N8: Q1.B, MIC1.pin1
  N9: LED1.cathode, R3.Pin_1
