# Fritzing sketch montage8 (saved by Fritzing 0.7.10b)
breadboards: 1

parts:
  U1 = atmega328 [package=dip]
  XTAL3 = Crystal [frequency="16 Mhz" package=THT]
  C1 = Ceramic Capacitor [capacitance=100nF package="100 mil [THT, multilayer]"]
  C2 = Ceramic Capacitor [capacitance=100nF package="100 mil [THT, multilayer]"]
  R1 = Resistor [tolerance=±5% resistance=10k package=THT]
  R2 = Resistor [tolerance=±5% resistance=1k package=THT]
  LED1 = LED - 5mm [color="Red (635nm)" package="5 mm [THT]"]
  R3 = Resistor [tolerance=±5% resistance=10k package=THT]
  R4 = Photocell (LDR) [package=THT]
  C11 = Electrolytic Capacitor [capacitance=1µF package="100 mil [THT, electrolytic]"]  # not connected
  C12 = Electrolytic Capacitor [capacitance=1µF package="100 mil [THT, electrolytic]"]  # not connected

nets:
  N1: U1.RESET, R1.Pin_1
  N2: U1.VCC, U1.AVCC, R1.Pin_0, R4.pin_1
  N3: U1.GND, C1.0, C2.0, R2.Pin_0, R3.Pin_1
  N4: U1.XLAT1, XTAL3.pin_0, C1.1
  N5: U1.XLAT2, XTAL3.pin_1, C2.1
  N6: U1.D10_(PWM), LED1.anode
  N7: U1.A5, R3.Pin_0, R4.pin_0
  N8: R2.Pin_1, LED1.cathode
